# Fritzing sketch eshift (saved by Fritzing 0.7.4b)
breadboards: 1

parts:
  Part1 = Arduino Pro Mini 3.3V
  Q1 = NPN-Transistor [part_number=BC639 package="TO92 [THT]"]
  R1 = Resistor [tolerance=±5% resistance=100 package=THT]
  J1 = Basic Servo
  R2 = Resistor [tolerance=±5% resistance=1k package=THT]
  R3 = Rotary Potentiometer (Small) [maximum_resistance=100kΩ]
  S1 = Pushbutton [package=THT]
  S2 = Pushbutton [package=THT]
  R4 = Resistor [tolerance=±5% resistance=10k package=THT]
  R5 = Resistor [tolerance=±5% resistance=10k package=THT]
  LED1 = LED - 3mm [color="Red (633nm)" package="3 mm [THT]"]
  C1 = Ceramic Capacitor [capacitance=0.1nF voltage=16V package="100 mil [THT, multilayer]"]

nets:
  GND: Part1.GND, Q1.E, R2.Pin_0, R3.leg1, S1.leg1, S2.leg1, C1.0
  5V: Part1.VCC, J1.vcc, R3.leg2, R4.Pin_1, R5.Pin_1, C1.1
  N1: Part1.A3, R3.wiper
  N2: Part1.D10, LED1.anode
  N3: Part1.D9, J1.pulse
  N4: Part1.D6, R1.Pin_0
  N5: Part1.D3, S2.leg0, R4.Pin_0
  N6: Part1.D2, S1.leg0, R5.Pin_0
  N7: Q1.B, J1.gnd
  N8: Q1.C, R1.Pin_1
  N9: R2.Pin_1, LED1.cathode

notes:
  Shift buttons
  Servo switch
  Trim potentiometer for servo calibration
